// Logisim project adder_subtractor.circ as structural Verilog: 1 circuit, main circuit main
module main (
  input  in_1,
  input  in_2,
  input  in_3,
  input  in_4,
  input  in_5,
  input  in_6,
  input  in_7,
  input  in_8,
  input  in_9,
  input  in_10
);

  wire and_1_out, and_2_out, and_3_out, and_4_out, and_5_out, and_6_out, not_1_out, not_2_out, not_3_out,
       or_1_out, or_2_out, xor_1_out, xor_2_out, xor_3_out, xor_4_out, xor_5_out, xor_6_out;

  and and_1 (and_1_out, xor_2_out, in_5);
  and and_2 (and_2_out, in_7, in_6);
  xor xor_1 (xor_1_out, in_1, in_3);
  LED led_1 (.in(xor_1_out));
  LED led_2 (.in(and_3_out));
  and and_3 (and_3_out, in_1, in_3);
  xor xor_2 (xor_2_out, in_7, in_6);
  or or_1 (or_1_out, and_1_out, and_2_out);
  xor xor_3 (xor_3_out, xor_2_out, in_5);
  LED led_3 (.in(xor_3_out));
  LED led_4 (.in(or_1_out));
  not not_1 (not_1_out, in_2);
  LED led_5 (.in(xor_4_out));
  xor xor_4 (xor_4_out, in_2, in_4);
  LED led_6 (.in(and_4_out));
  and and_4 (and_4_out, not_1_out, in_4);
  not not_2 (not_2_out, in_10);
  not not_3 (not_3_out, xor_5_out);
  xor xor_5 (xor_5_out, in_10, in_9);
  and and_5 (and_5_out, not_2_out, in_9);
  and and_6 (and_6_out, in_8, not_3_out);
  xor xor_6 (xor_6_out, xor_5_out, in_8);
  LED led_7 (.in(xor_6_out));
  LED led_8 (.in(or_2_out));
  or or_2 (or_2_out, and_5_out, and_6_out);

  // Notes on the sheet:
  //   Half Adder,Full Adder,Half Subtractor,Full Subtractor
endmodule
