// Logisim project encoder_decoder.circ as structural Verilog: 1 circuit, main circuit main
module main (
  input  in_1,
  input  in_2,
  input  in_3,
  input  in_4,
  input  in_5,
  input  in_6,
  input  in_7,
  input  in_8,
  input  in_9,
  input  in_10,
  input  in_11,
  input  in_12
);

  wire and_1_out, and_2_out, and_3_out, and_4_out, and_5_out, and_6_out, and_7_out, and_8_out, not_1_out,
       not_2_out, not_3_out, or_1_out, or_2_out, or_3_out;

  LED led_1 (.in(or_1_out));
  or or_1 (or_1_out, in_7, in_5, in_3, in_1);
  LED led_2 (.in(or_2_out));
  or or_2 (or_2_out, in_6, in_5, in_2, in_1);
  or or_3 (or_3_out, in_4, in_3, in_2, in_1);
  LED led_3 (.in(or_3_out));
  not not_1 (not_1_out, in_10);
  not not_2 (not_2_out, in_11);
  not not_3 (not_3_out, in_12);
  and and_1 (and_1_out, not_1_out, not_2_out, not_3_out, in_9);
  LED led_4 (.in(and_1_out));
  LED led_5 (.in(and_2_out));
  and and_2 (and_2_out, not_1_out, not_2_out, in_12, in_9);
  LED led_6 (.in(and_3_out));
  and and_3 (and_3_out, not_1_out, in_11, not_3_out, in_9);
  and and_4 (and_4_out, not_1_out, in_11, in_12, in_9);
  LED led_7 (.in(and_4_out));
  and and_5 (and_5_out, in_10, not_2_out, not_3_out, in_9);
  LED led_8 (.in(and_5_out));
  LED led_9 (.in(and_6_out));
  and and_6 (and_6_out, in_10, not_2_out, in_12, in_9);
  and and_7 (and_7_out, in_10, in_11, not_3_out, in_9);
  LED led_10 (.in(and_7_out));
  and and_8 (and_8_out, in_10, in_11, in_12, in_9);
  LED led_11 (.in(and_8_out));

  // Notes on the sheet:
  //   D7 TO D0 =>
  //   Y0
  //   Y1
  //   Y2
  //   E , Y2 , Y1 , Y0
endmodule
