// Logisim project mux_demux.circ as structural Verilog: 1 circuit, main circuit main
module main (
  input  in_1,
  input  in_2,
  input  in_3,
  input  in_4,
  input  in_5,
  input  in_6
);

  wire and_1_out, and_2_out, and_3_out, and_4_out, and_5_out, and_6_out, and_7_out, and_8_out, and_9_out,
       and_10_out, and_11_out, and_12_out, and_13_out, and_14_out, and_15_out, and_16_out, not_1_out,
       not_2_out, not_3_out, not_4_out, not_5_out, not_6_out, or_1_out;

  not not_1 (not_1_out, in_1);
  not not_2 (not_2_out, in_2);
  not not_3 (not_3_out, in_3);
  and and_1 (and_1_out, not_1_out, not_2_out, not_3_out);
  and and_2 (and_2_out, not_1_out, not_2_out, in_3);
  and and_3 (and_3_out, not_1_out, in_2, not_3_out);
  and and_4 (and_4_out, not_1_out, in_2, in_3);
  and and_5 (and_5_out, in_1, not_2_out, not_3_out);
  and and_6 (and_6_out, in_1, not_2_out, in_3);
  and and_7 (and_7_out, in_1, in_2, not_3_out);
  and and_8 (and_8_out, in_1, in_2, in_3);
  or or_1 (or_1_out, and_1_out, and_2_out, and_3_out, and_4_out, and_5_out, and_6_out, and_7_out, and_8_out);
  LED led_1 (.in(or_1_out));
  not not_4 (not_4_out, in_4);
  not not_5 (not_5_out, in_5);
  not not_6 (not_6_out, in_6);
  and and_9 (and_9_out, not_4_out, not_5_out, not_6_out);
  and and_10 (and_10_out, not_4_out, not_5_out, in_6);
  and and_11 (and_11_out, not_4_out, in_5, not_6_out);
  and and_12 (and_12_out, not_4_out, in_5, in_6);
  and and_13 (and_13_out, in_4, not_5_out, not_6_out);
  and and_14 (and_14_out, in_4, not_5_out, in_6);
  and and_15 (and_15_out, in_4, in_5, not_6_out);
  and and_16 (and_16_out, in_4, in_5, in_6);
  LED led_2 (.in(and_9_out));
  LED led_3 (.in(and_10_out));
  LED led_4 (.in(and_11_out));
  LED led_5 (.in(and_12_out));
  LED led_6 (.in(and_13_out));
  LED led_7 (.in(and_14_out));
  LED led_8 (.in(and_15_out));
  LED led_9 (.in(and_16_out));
endmodule
