// Logisim project priority_encoder.circ as structural Verilog: 1 circuit, main circuit main
module main (
  input  in_1,
  input  in_2,
  input  in_3
);

  wire and_1_out, not_1_out, or_1_out, or_2_out;

  not not_1 (not_1_out, in_2);
  and and_1 (and_1_out, in_1, not_1_out);
  or or_1 (or_1_out, and_1_out, in_3);
  or or_2 (or_2_out, in_2, in_3);
  LED led_1 (.in(or_1_out));
  LED led_2 (.in(or_2_out));

  // Notes on the sheet:
  //   i1,i2,i3 downwards
endmodule
